// Logisim project 2031346642-Bushra-Hossain-Task-6.circ as structural Verilog: 10 circuits, main circuit main
module main (
);


  // Notes on the sheet:
  //                                                                                                                   Name: Bushra Hossain                       NSU ID : 203 1346  642 
endmodule

module _1bit_Logic_Unit (
  input  A,
  input  B,
  input  [1:0] S1_S0,
  output F
);

  wire and_1_out, not_1_out, or_1_out, xor_1_out;

  and and_1 (and_1_out, A, B);
  or or_1 (or_1_out, A, B);
  xor xor_1 (xor_1_out, A, B);
  not not_1 (not_1_out, A);
  Multiplexer #(.select(2), .enable("false")) multiplexer_1 (
    .in0(and_1_out), .in1(or_1_out), .in2(xor_1_out), .in3(not_1_out), .out(F), .sel(S1_S0));

  // Notes on the sheet:
  //                                                         Figure 2: 1-bit Logic Unit
endmodule

module _2bit_Logic_Unit (
  input  [1:0] A1A0,
  input  [1:0] B1B0,
  input  [1:0] s1s0,
  output [1:0] F1F0
);

  _1bit_Logic_Unit u_1bit_logic_unit_1 (.A(A1A0[0]), .B(B1B0[0]), .S1_S0(s1s0), .F(F1F0[0]));
  _1bit_Logic_Unit u_1bit_logic_unit_2 (.A(A1A0[1]), .B(B1B0[1]), .S1_S0(s1s0), .F(F1F0[1]));

  // Notes on the sheet:
  //                                                Figure 3: 2-bit Logic Unit using 1-bit logic unit circuit
endmodule

module _1_bit_AU (
  input  Cin,
  input  [1:0] S1S0,
  input  A,
  input  B,
  output D,
  output Cout
);

  wire multiplexer_1_out, not_1_out;

  not not_1 (not_1_out, B);
  Multiplexer #(.select(2), .enable("false")) multiplexer_1 (
    .in0(B), .in1(not_1_out), .in2(1'b0), .in3(1'b1), .out(multiplexer_1_out), .sel(S1S0));
  Adder #(.width(1)) adder_1 (.a(A), .b(multiplexer_1_out), .out(D), .cin(Cin), .cout(Cout));

  // Notes on the sheet:
  //                     figure: 1 bit AU
endmodule

module _2_bit_AU (
  input  Cin,
  input  [1:0] S1S0,
  input  [1:0] A1A0,
  input  [1:0] B1B0,
  output [1:0] D1D0,
  output Cout
);

  wire _0_cout;

  _1_bit_AU _0 (.Cin(Cin), .D(D1D0[0]), .Cout(_0_cout), .S1S0(S1S0), .A(A1A0[0]), .B(B1B0[0]));
  _1_bit_AU _1 (.Cin(_0_cout), .D(D1D0[1]), .Cout(Cout), .S1S0(S1S0), .A(A1A0[1]), .B(B1B0[1]));

  // Notes on the sheet:
  //   Figure: 2 bit AU
endmodule

module _4_bit_multiplication_unit (
  input  [3:0] B,
  input  [3:0] A,
  output [7:0] P
);

  wire [2:0] and_14_out;
  wire [3:0] adder_2_cout, adder_3_out, and_3_out, and_7_out, and_12_out;

  and and_1 (and_3_out[2], A[3], B[2]);
  and and_2 (and_3_out[3], A[3], B[3]);
  and and_3 (and_3_out[0], A[3], B[0]);
  and and_4 (and_3_out[1], A[3], B[1]);
  and and_5 (and_7_out[2], B[2], A[2]);
  and and_6 (and_7_out[3], B[3], A[2]);
  and and_7 (and_7_out[0], B[0], A[2]);
  and and_8 (and_7_out[1], B[1], A[2]);
  and and_9 (and_12_out[2], A[1], B[2]);
  and and_10 (and_12_out[3], A[1], B[3]);
  and and_11 (and_12_out[1], A[1], B[1]);
  and and_12 (and_12_out[0], A[1], B[0]);
  Adder #(.width(4)) adder_1 (.a(adder_2_cout), .b(and_3_out), .out(P[6:3]), .cin(1'b0), .cout(P[7]));
  and and_13 (and_14_out[2], A[0], B[3]);
  Adder #(.width(4)) adder_2 (
    .a(adder_3_out), .b(and_7_out), .out({adder_2_cout[2:0], P[2]}), .cin(1'b0), .cout(adder_2_cout[3]));
  and and_14 (and_14_out[0], A[0], B[1]);
  and and_15 (and_14_out[1], A[0], B[2]);
  and and_16 (P[0], A[0], B[0]);
  Adder #(.width(4)) adder_3 (
    .a({1'b0, and_14_out}), .b(and_12_out), .out({adder_3_out[2:0], P[1]}), .cin(1'b0), .cout(adder_3_out[3]));

  // Notes on the sheet:
  //                                                            Figure : A 4bit by 4bit Multiplication Unit
endmodule

module _16_BITS_REGISTER (
  input  [15:0] Write_Data,
  input  [3:0] Read_Register_1___RS,
  input  [3:0] Read_Register_2__RT,
  input  [3:0] Write_Register_RD,
  input  Register_Write,
  input  CLK,
  output [15:0] Read_Data_1,
  output [15:0] Read_Data_2
);

  wire and_1_out, and_2_out, and_3_out, and_4_out, and_5_out, and_6_out, and_7_out, and_8_out, and_9_out,
       and_10_out, and_11_out, and_12_out, and_13_out, and_14_out, and_15_out, and_16_out, decoder_1_out0,
       decoder_1_out1, decoder_1_out2, decoder_1_out3, decoder_1_out4, decoder_1_out5, decoder_1_out6,
       decoder_1_out7, decoder_1_out8, decoder_1_out9, decoder_1_out10, decoder_1_out11, decoder_1_out12,
       decoder_1_out13, decoder_1_out14, decoder_1_out15;
  wire [15:0] R0_q, R1_q, R2_q, R3_q, R4_q, R5_q, R6_q, R7_q, R8_q, R9_q, R10_q, R11_q, R12_q, R13_q, R14_q,
       R15_q, undriven;

  Decoder #(.select(4), .enable("false")) decoder_1 (
    .out0(decoder_1_out0), .out1(decoder_1_out1), .out2(decoder_1_out2), .out3(decoder_1_out3),
    .out4(decoder_1_out4), .out5(decoder_1_out5), .out6(decoder_1_out6), .out7(decoder_1_out7),
    .out8(decoder_1_out8), .out9(decoder_1_out9), .out10(decoder_1_out10), .out11(decoder_1_out11),
    .out12(decoder_1_out12), .out13(decoder_1_out13), .out14(decoder_1_out14), .out15(decoder_1_out15),
    .sel(Write_Register_RD));
  and and_1 (and_1_out, decoder_1_out0, Register_Write);
  and and_2 (and_2_out, decoder_1_out1, Register_Write);
  and and_3 (and_3_out, decoder_1_out2, Register_Write);
  and and_4 (and_4_out, decoder_1_out3, Register_Write);
  and and_5 (and_5_out, Register_Write, decoder_1_out4);
  and and_6 (and_6_out, Register_Write, decoder_1_out5);
  and and_7 (and_7_out, Register_Write, decoder_1_out6);
  and and_8 (and_8_out, Register_Write, decoder_1_out7);
  and and_9 (and_9_out, Register_Write, decoder_1_out8);
  and and_10 (and_10_out, Register_Write, decoder_1_out9);
  and and_11 (and_11_out, Register_Write, decoder_1_out10);
  and and_12 (and_12_out, Register_Write, decoder_1_out11);
  and and_13 (and_13_out, Register_Write, decoder_1_out12);
  and and_14 (and_14_out, Register_Write, decoder_1_out13);
  and and_15 (and_15_out, Register_Write, decoder_1_out14);
  and and_16 (and_16_out, Register_Write, decoder_1_out15);
  Register #(.width(16)) R0 (.D(Write_Data), .en(and_1_out), .Q(R0_q), .clk(CLK));  // open: clr
  Register #(.width(16)) R1 (.D(Write_Data), .en(and_2_out), .Q(R1_q), .clk(CLK));  // open: clr
  Register #(.width(16)) R2 (.D(Write_Data), .en(and_3_out), .Q(R2_q), .clk(CLK));  // open: clr
  Register #(.width(16)) R3 (.D(Write_Data), .en(and_4_out), .Q(R3_q), .clk(CLK));  // open: clr
  Register #(.width(16)) R4 (.D(Write_Data), .en(and_5_out), .Q(R4_q), .clk(CLK));  // open: clr
  Register #(.width(16)) R5 (.D(Write_Data), .en(and_6_out), .Q(R5_q), .clk(CLK));  // open: clr
  Register #(.width(16)) R6 (.D(Write_Data), .en(and_7_out), .Q(R6_q), .clk(CLK));  // open: clr
  Register #(.width(16)) R7 (.D(Write_Data), .en(and_8_out), .Q(R7_q), .clk(CLK));  // open: clr
  Register #(.width(16)) R8 (.D(undriven), .en(and_9_out), .Q(R8_q), .clk(CLK));  // open: clr
  Register #(.width(16)) R9 (.D(undriven), .en(and_10_out), .Q(R9_q), .clk(CLK));  // open: clr
  Register #(.width(16)) R10 (.D(undriven), .en(and_11_out), .Q(R10_q), .clk(CLK));  // open: clr
  Register #(.width(16)) R11 (.D(undriven), .en(and_12_out), .Q(R11_q), .clk(CLK));  // open: clr
  Register #(.width(16)) R12 (.D(undriven), .en(and_13_out), .Q(R12_q), .clk(CLK));  // open: clr
  Register #(.width(16)) R13 (.D(undriven), .en(and_14_out), .Q(R13_q), .clk(CLK));  // open: clr
  Register #(.width(16)) R14 (.D(undriven), .en(and_15_out), .Q(R14_q), .clk(CLK));  // open: clr
  Register #(.width(16)) R15 (.D(undriven), .en(and_16_out), .Q(R15_q), .clk(CLK));  // open: clr
  Multiplexer #(.select(4), .width(16), .enable("false")) multiplexer_1 (
    .in0(R0_q), .in1(R1_q), .in2(R2_q), .in3(R3_q), .in4(R4_q), .in5(R5_q), .in6(R6_q), .in7(R7_q),
    .in8(R8_q), .in9(R9_q), .in10(R10_q), .in11(R11_q), .in12(R12_q), .in13(R13_q), .in14(R14_q),
    .in15(R15_q), .out(Read_Data_1), .sel(Read_Register_1___RS));
  Multiplexer #(.select(4), .width(16), .enable("false")) multiplexer_2 (
    .in0(R0_q), .in1(R1_q), .in2(R2_q), .in3(R3_q), .in4(R4_q), .in5(R5_q), .in6(R6_q), .in7(R7_q),
    .in8(R8_q), .in9(R9_q), .in10(R10_q), .in11(R11_q), .in12(R12_q), .in13(R13_q), .in14(R14_q),
    .in15(R15_q), .out(Read_Data_2), .sel(Read_Register_2__RT));
endmodule

// IFU
module Intruction_Fetch_Unit (
  input  cLK,
  output [15:0] out_2
);

  wire [1:0] adder_1_out, register_1_q;

  Register #(.width(2)) register_1 (.D(adder_1_out), .Q(register_1_q), .clk(cLK));  // open: en, clr
  Adder #(.width(2)) adder_1 (.a(2'b01), .b(register_1_q), .out(adder_1_out), .cin(1'b0));  // open: cout
  ROM #(.addrWidth(2), .dataWidth(16)) rom_1 (.addr(register_1_q), .data(out_2));  // open: sel

  // Notes on the sheet:
  //   ROM (Inst. Memory)
  //   contents of rom_1 (hex, n*v repeats v):
  //   123
endmodule

module R_trype (
  input  in_1,
  input  clk,
  output [3:0] Opcode,
  output [3:0] Rs,
  output [3:0] Rt,
  output [3:0] Rd,
  output [15:0] out_7
);

  wire [1:0] bit_extender_1_out;
  wire [15:0] n16_bits_register_1_read_data_1, n16_bits_register_1_read_data_2;

  Intruction_Fetch_Unit intruction_fetch_unit_1 (.cLK(clk), .out_2({Opcode, Rs, Rt, Rd}));
  Bit_Extender #(.in_width(4), .out_width(2)) bit_extender_1 (.in(Opcode), .out(bit_extender_1_out));
  ALU alu_1 (
    .A(n16_bits_register_1_read_data_1), .B(n16_bits_register_1_read_data_2), .ALU_op(bit_extender_1_out),
    .B_inv(in_1), .C_in(in_1), .Result(out_7));  // open: C_out
  _16_BITS_REGISTER u_16_bits_register_1 (
    .Write_Data(out_7), .Read_Data_1(n16_bits_register_1_read_data_1),
    .Read_Data_2(n16_bits_register_1_read_data_2), .Write_Register_RD(Rd), .Register_Write(1'b1), .CLK(clk),
    .Read_Register_2__RT(Rt), .Read_Register_1___RS(Rs));
endmodule

module ALU (
  input  [15:0] A,
  input  C_in,
  input  [15:0] B,
  input  [1:0] ALU_op,
  input  B_inv,
  output [15:0] Result,
  output C_out
);

  wire [15:0] adder_1_out, adder_2_out, and_1_out, multiplexer_1_out, not_1_out, or_1_out;

  Multiplexer #(.width(16), .enable("false")) multiplexer_1 (
    .in0(B), .in1(not_1_out), .out(multiplexer_1_out), .sel(B_inv));
  assign not_1_out = ~B;  // NOT_Gate not_1, 16 bits wide
  Adder #(.width(16)) adder_1 (.a(A), .b(multiplexer_1_out), .out(adder_1_out));  // open: cin, cout
  Adder #(.width(16)) adder_2 (.a(A), .b(multiplexer_1_out), .out(adder_2_out), .cin(C_in), .cout(C_out));
  assign and_1_out = A & multiplexer_1_out;  // AND_Gate and_1, 16 bits wide
  assign or_1_out = A | multiplexer_1_out;  // OR_Gate or_1, 16 bits wide
  Multiplexer #(.select(2), .width(16), .enable("false")) multiplexer_2 (
    .in0(adder_1_out), .in1(adder_2_out), .in2(and_1_out), .in3(or_1_out), .out(Result), .sel(ALU_op));
endmodule
