// Logisim project 16 bit alu (ISA).circ as structural Verilog: 5 circuits, main circuit main
// 16 bit regester
module _16_bit_regester (
  input  [15:0] Data_in,
  input  [3:0] rs,
  input  [3:0] rd,
  input  unable,
  input  [3:0] rt,
  input  Clock,
  output [15:0] Data_out_1,
  output [15:0] Data_out_2
);

  wire and_1_out, and_2_out, and_3_out, and_4_out, and_5_out, and_6_out, and_7_out, and_8_out, and_9_out,
       and_10_out, and_11_out, and_12_out, and_13_out, and_14_out, and_15_out, and_16_out, decoder_1_out0,
       decoder_1_out1, decoder_1_out2, decoder_1_out3, decoder_1_out4, decoder_1_out5, decoder_1_out6,
       decoder_1_out7, decoder_1_out8, decoder_1_out9, decoder_1_out10, decoder_1_out11, decoder_1_out12,
       decoder_1_out13, decoder_1_out14, decoder_1_out15;
  wire [15:0] R0_q, R1_q, R2_q, R3_q, R4_q, R5_q, R6_q, R7_q, R8_q, R9_q, R10_q, R11_q, R12_q, R13_q, R14_q,
       R15_q;

  Decoder #(.select(4), .enable("false")) decoder_1 (
    .out0(decoder_1_out0), .out1(decoder_1_out1), .out2(decoder_1_out2), .out3(decoder_1_out3),
    .out4(decoder_1_out4), .out5(decoder_1_out5), .out6(decoder_1_out6), .out7(decoder_1_out7),
    .out8(decoder_1_out8), .out9(decoder_1_out9), .out10(decoder_1_out10), .out11(decoder_1_out11),
    .out12(decoder_1_out12), .out13(decoder_1_out13), .out14(decoder_1_out14), .out15(decoder_1_out15),
    .sel(rd));
  and and_1 (and_1_out, decoder_1_out0, unable);
  and and_2 (and_2_out, decoder_1_out1, unable);
  and and_3 (and_3_out, decoder_1_out2, unable);
  and and_4 (and_4_out, decoder_1_out3, unable);
  and and_5 (and_5_out, decoder_1_out4, unable);
  and and_6 (and_6_out, decoder_1_out5, unable);
  and and_7 (and_7_out, decoder_1_out6, unable);
  and and_8 (and_8_out, decoder_1_out7, unable);
  Register #(.width(16)) R0 (.D(Data_in), .en(and_1_out), .Q(R0_q), .clk(Clock));  // open: clr
  Register #(.width(16)) R1 (.D(Data_in), .en(and_2_out), .Q(R1_q), .clk(Clock));  // open: clr
  Register #(.width(16)) R2 (.D(Data_in), .en(and_3_out), .Q(R2_q), .clk(Clock));  // open: clr
  Register #(.width(16)) R3 (.D(Data_in), .en(and_4_out), .Q(R3_q), .clk(Clock));  // open: clr
  Register #(.width(16)) R4 (.D(Data_in), .en(and_5_out), .Q(R4_q), .clk(Clock));  // open: clr
  Register #(.width(16)) R5 (.D(Data_in), .en(and_6_out), .Q(R5_q), .clk(Clock));  // open: clr
  Register #(.width(16)) R6 (.D(Data_in), .en(and_7_out), .Q(R6_q), .clk(Clock));  // open: clr
  Register #(.width(16)) R7 (.D(Data_in), .en(and_8_out), .Q(R7_q), .clk(Clock));  // open: clr
  and and_9 (and_9_out, decoder_1_out8, unable);
  and and_10 (and_10_out, decoder_1_out9, unable);
  and and_11 (and_11_out, decoder_1_out10, unable);
  and and_12 (and_12_out, decoder_1_out11, unable);
  and and_13 (and_13_out, decoder_1_out12, unable);
  and and_14 (and_14_out, decoder_1_out13, unable);
  and and_15 (and_15_out, decoder_1_out14, unable);
  and and_16 (and_16_out, decoder_1_out15, unable);
  Register #(.width(16)) R8 (.D(Data_in), .en(and_9_out), .Q(R8_q), .clk(Clock));  // open: clr
  Register #(.width(16)) R9 (.D(Data_in), .en(and_10_out), .Q(R9_q), .clk(Clock));  // open: clr
  Register #(.width(16)) R10 (.D(Data_in), .en(and_11_out), .Q(R10_q), .clk(Clock));  // open: clr
  Register #(.width(16)) R11 (.D(Data_in), .en(and_12_out), .Q(R11_q), .clk(Clock));  // open: clr
  Register #(.width(16)) R12 (.D(Data_in), .en(and_13_out), .Q(R12_q), .clk(Clock));  // open: clr
  Register #(.width(16)) R13 (.D(Data_in), .en(and_14_out), .Q(R13_q), .clk(Clock));  // open: clr
  Register #(.width(16)) R14 (.D(Data_in), .en(and_15_out), .Q(R14_q), .clk(Clock));  // open: clr
  Register #(.width(16)) R15 (.D(Data_in), .en(and_16_out), .Q(R15_q), .clk(Clock));  // open: clr
  Multiplexer #(.select(4), .width(16), .enable("false")) multiplexer_1 (
    .in0(R0_q), .in1(R1_q), .in2(R2_q), .in3(R3_q), .in4(R4_q), .in5(R5_q), .in6(R6_q), .in7(R7_q),
    .in8(R8_q), .in9(R9_q), .in10(R10_q), .in11(R11_q), .in12(R12_q), .in13(R13_q), .in14(R14_q),
    .in15(R15_q), .out(Data_out_1), .sel(rs));
  Multiplexer #(.select(4), .width(16), .enable("false")) multiplexer_2 (
    .in0(R0_q), .in1(R1_q), .in2(R2_q), .in3(R3_q), .in4(R4_q), .in5(R5_q), .in6(R6_q), .in7(R7_q),
    .in8(R8_q), .in9(R9_q), .in10(R10_q), .in11(R11_q), .in12(R12_q), .in13(R13_q), .in14(R14_q),
    .in15(R15_q), .out(Data_out_2), .sel(rt));

  // Notes on the sheet:
  //   Md. Ishtiaq Ahamed Fahim 2012518642
endmodule

module main (
  input  On,
  output [5:0] opcode,
  output [4:0] rs,
  output [4:0] rt,
  output [4:0] rd,
  output [4:0] sa,
  output [5:0] \function ,
  output [15:0] out_8,
  output [15:0] out_9,
  output [15:0] out_10
);

  wire and_1_out, Clock_out, not_1_out;
  wire [15:0] adder_1_out, bit_extender_1_out, register_1_q;

  Clock Clock (.out(Clock_out));
  and and_1 (and_1_out, Clock_out, On);
  not not_1 (not_1_out, On);
  Adder #(.width(16)) adder_1 (.a(register_1_q), .b(bit_extender_1_out), .out(adder_1_out));  // open: cin, cout
  assign bit_extender_1_out = {{15{1'b0}}, On};  // Bit_Extender bit_extender_1
  ROM #(.addrWidth(16), .dataWidth(32)) rom_1 (
    .addr(register_1_q), .data({opcode, rs, rt, rd, sa, \function }), .sel(On));
  Register #(.width(16)) register_1 (.D(adder_1_out), .Q(register_1_q), .clk(and_1_out), .clr(not_1_out));  // open: en
  _32_bit_register u_32_bit_register_1 (
    .Data_in(out_10), .Unable(On), .Clock(and_1_out), .rs(rs), .rt(rt), .rd(rd), .Data_out_2(out_9),
    .Data_out_1(out_8));  // open: Clear
  ALU alu_1 (.Data_in_1(out_8), .Data_in_2(out_9), .Select_bit(\function ), .Data_out(out_10));

  // Notes on the sheet:
  //   contents of rom_1 (hex, n*v repeats v):
  //   11020 11022 11024 11025
endmodule

// 32 register
module _32_bit_register (
  input  [15:0] Data_in,
  input  Unable,
  input  Clock,
  input  Clear,
  input  [4:0] rs,
  input  [4:0] rt,
  input  [4:0] rd,
  output [15:0] Data_out_1,
  output [15:0] Data_out_2
);

  wire decoder_1_out0, decoder_1_out1, decoder_1_out2, decoder_1_out3, decoder_1_out4, decoder_1_out5,
       decoder_1_out6, decoder_1_out7, decoder_1_out8, decoder_1_out9, decoder_1_out10, decoder_1_out11,
       decoder_1_out12, decoder_1_out13, decoder_1_out14, decoder_1_out15, decoder_1_out16, decoder_1_out17,
       decoder_1_out18, decoder_1_out19, decoder_1_out20, decoder_1_out21, decoder_1_out22, decoder_1_out23,
       decoder_1_out24, decoder_1_out25, decoder_1_out26, decoder_1_out27, decoder_1_out28, decoder_1_out29,
       decoder_1_out30, decoder_1_out31;
  wire [15:0] register_1_q, register_2_q, register_3_q, register_4_q, register_5_q, register_6_q,
       register_7_q, register_8_q, register_9_q, register_10_q, register_11_q, register_12_q, register_13_q,
       register_14_q, register_15_q, register_16_q, register_17_q, register_18_q, register_19_q,
       register_20_q, register_21_q, register_22_q, register_23_q, register_24_q, register_25_q,
       register_26_q, register_27_q, register_28_q, register_29_q, register_30_q, register_31_q,
       register_32_q;

  Decoder #(.select(5)) decoder_1 (
    .out0(decoder_1_out0), .out1(decoder_1_out1), .out2(decoder_1_out2), .out3(decoder_1_out3),
    .out4(decoder_1_out4), .out5(decoder_1_out5), .out6(decoder_1_out6), .out7(decoder_1_out7),
    .out8(decoder_1_out8), .out9(decoder_1_out9), .out10(decoder_1_out10), .out11(decoder_1_out11),
    .out12(decoder_1_out12), .out13(decoder_1_out13), .out14(decoder_1_out14), .out15(decoder_1_out15),
    .out16(decoder_1_out16), .out17(decoder_1_out17), .out18(decoder_1_out18), .out19(decoder_1_out19),
    .out20(decoder_1_out20), .out21(decoder_1_out21), .out22(decoder_1_out22), .out23(decoder_1_out23),
    .out24(decoder_1_out24), .out25(decoder_1_out25), .out26(decoder_1_out26), .out27(decoder_1_out27),
    .out28(decoder_1_out28), .out29(decoder_1_out29), .out30(decoder_1_out30), .out31(decoder_1_out31),
    .sel(rd), .en(Unable));
  Register #(.width(16)) register_1 (.D(Data_in), .en(decoder_1_out0), .Q(register_1_q), .clk(Clock), .clr(Clear));
  Register #(.width(16)) register_2 (.D(Data_in), .en(decoder_1_out1), .Q(register_2_q), .clk(Clock), .clr(Clear));
  Register #(.width(16)) register_3 (.D(Data_in), .en(decoder_1_out2), .Q(register_3_q), .clk(Clock), .clr(Clear));
  Register #(.width(16)) register_4 (.D(Data_in), .en(decoder_1_out3), .Q(register_4_q), .clk(Clock), .clr(Clear));
  Register #(.width(16)) register_5 (.D(Data_in), .en(decoder_1_out4), .Q(register_5_q), .clk(Clock), .clr(Clear));
  Register #(.width(16)) register_6 (.D(Data_in), .en(decoder_1_out5), .Q(register_6_q), .clk(Clock), .clr(Clear));
  Register #(.width(16)) register_7 (.D(Data_in), .en(decoder_1_out6), .Q(register_7_q), .clk(Clock), .clr(Clear));
  Register #(.width(16)) register_8 (.D(Data_in), .en(decoder_1_out7), .Q(register_8_q), .clk(Clock), .clr(Clear));
  Register #(.width(16)) register_9 (.D(Data_in), .en(decoder_1_out8), .Q(register_9_q), .clk(Clock), .clr(Clear));
  Register #(.width(16)) register_10 (.D(Data_in), .en(decoder_1_out9), .Q(register_10_q), .clk(Clock), .clr(Clear));
  Register #(.width(16)) register_11 (.D(Data_in), .en(decoder_1_out10), .Q(register_11_q), .clk(Clock), .clr(Clear));
  Register #(.width(16)) register_12 (.D(Data_in), .en(decoder_1_out11), .Q(register_12_q), .clk(Clock), .clr(Clear));
  Register #(.width(16)) register_13 (.D(Data_in), .en(decoder_1_out12), .Q(register_13_q), .clk(Clock), .clr(Clear));
  Register #(.width(16)) register_14 (.D(Data_in), .en(decoder_1_out13), .Q(register_14_q), .clk(Clock), .clr(Clear));
  Register #(.width(16)) register_15 (.D(Data_in), .en(decoder_1_out14), .Q(register_15_q), .clk(Clock), .clr(Clear));
  Register #(.width(16)) register_16 (.D(Data_in), .en(decoder_1_out15), .Q(register_16_q), .clk(Clock), .clr(Clear));
  Register #(.width(16)) register_17 (.D(Data_in), .en(decoder_1_out16), .Q(register_17_q), .clk(Clock), .clr(Clear));
  Register #(.width(16)) register_18 (.D(Data_in), .en(decoder_1_out17), .Q(register_18_q), .clk(Clock), .clr(Clear));
  Register #(.width(16)) register_19 (.D(Data_in), .en(decoder_1_out18), .Q(register_19_q), .clk(Clock), .clr(Clear));
  Register #(.width(16)) register_20 (.D(Data_in), .en(decoder_1_out19), .Q(register_20_q), .clk(Clock), .clr(Clear));
  Register #(.width(16)) register_21 (.D(Data_in), .en(decoder_1_out20), .Q(register_21_q), .clk(Clock), .clr(Clear));
  Register #(.width(16)) register_22 (.D(Data_in), .en(decoder_1_out21), .Q(register_22_q), .clk(Clock), .clr(Clear));
  Register #(.width(16)) register_23 (.D(Data_in), .en(decoder_1_out22), .Q(register_23_q), .clk(Clock), .clr(Clear));
  Register #(.width(16)) register_24 (.D(Data_in), .en(decoder_1_out23), .Q(register_24_q), .clk(Clock), .clr(Clear));
  Multiplexer #(.select(5), .width(16), .enable("false")) multiplexer_1 (
    .in0(register_1_q), .in1(register_2_q), .in2(register_3_q), .in3(register_4_q), .in4(register_5_q),
    .in5(register_6_q), .in6(register_7_q), .in7(register_8_q), .in8(register_9_q), .in9(register_10_q),
    .in10(register_11_q), .in11(register_12_q), .in12(register_13_q), .in13(register_14_q),
    .in14(register_15_q), .in15(register_16_q), .in16(register_17_q), .in17(register_18_q),
    .in18(register_19_q), .in19(register_20_q), .in20(register_21_q), .in21(register_22_q),
    .in22(register_23_q), .in23(register_24_q), .in24(register_25_q), .in25(register_26_q),
    .in26(register_27_q), .in27(register_28_q), .in28(register_29_q), .in29(register_30_q),
    .in30(register_31_q), .in31(register_32_q), .out(Data_out_1), .sel(rs));
  Register #(.width(16)) register_25 (.D(Data_in), .en(decoder_1_out24), .Q(register_25_q), .clk(Clock), .clr(Clear));
  Register #(.width(16)) register_26 (.D(Data_in), .en(decoder_1_out25), .Q(register_26_q), .clk(Clock), .clr(Clear));
  Register #(.width(16)) register_27 (.D(Data_in), .en(decoder_1_out26), .Q(register_27_q), .clk(Clock), .clr(Clear));
  Register #(.width(16)) register_28 (.D(Data_in), .en(decoder_1_out27), .Q(register_28_q), .clk(Clock), .clr(Clear));
  Register #(.width(16)) register_29 (.D(Data_in), .en(decoder_1_out28), .Q(register_29_q), .clk(Clock), .clr(Clear));
  Register #(.width(16)) register_30 (.D(Data_in), .en(decoder_1_out29), .Q(register_30_q), .clk(Clock), .clr(Clear));
  Register #(.width(16)) register_31 (.D(Data_in), .en(decoder_1_out30), .Q(register_31_q), .clk(Clock), .clr(Clear));
  Register #(.width(16)) register_32 (.D(Data_in), .en(decoder_1_out31), .Q(register_32_q), .clk(Clock), .clr(Clear));
  Multiplexer #(.select(5), .width(16), .enable("false")) multiplexer_2 (
    .in0(register_1_q), .in1(register_2_q), .in2(register_3_q), .in3(register_4_q), .in4(register_5_q),
    .in5(register_6_q), .in6(register_7_q), .in7(register_8_q), .in8(register_9_q), .in9(register_10_q),
    .in10(register_11_q), .in11(register_12_q), .in12(register_13_q), .in13(register_14_q),
    .in14(register_15_q), .in15(register_16_q), .in16(register_17_q), .in17(register_18_q),
    .in18(register_19_q), .in19(register_20_q), .in20(register_21_q), .in21(register_22_q),
    .in22(register_23_q), .in23(register_24_q), .in24(register_25_q), .in25(register_26_q),
    .in26(register_27_q), .in27(register_28_q), .in28(register_29_q), .in29(register_30_q),
    .in30(register_31_q), .in31(register_32_q), .out(Data_out_2), .sel(rt));
endmodule

module ALU (
  input  [15:0] Data_in_1,
  input  [15:0] Data_in_2,
  input  [5:0] Select_bit,
  output [15:0] Data_out
);

  wire [15:0] adder_1_out, and_1_out, divider_1_out, multiplexer_1_out, multiplexer_2_out, multiplier_1_out,
       or_1_out, subtractor_1_out, xor_1_out;

  DotMatrix #(.inputtype("row"), .matrixrows(1)) dotmatrix_1 (.row0(Select_bit[5:1]));
  Multiplier #(.width(16)) multiplier_1 (.a(Data_in_1), .b(Data_in_2), .out(multiplier_1_out));  // open: cin, cout
  Divider #(.width(16)) divider_1 (.a(Data_in_1), .b(Data_in_2), .out(divider_1_out));  // open: upper, rem
  Adder #(.width(16)) adder_1 (.a(Data_in_1), .b(Data_in_2), .out(adder_1_out));  // open: cin, cout
  Subtractor #(.width(16)) subtractor_1 (.a(Data_in_1), .b(Data_in_2), .out(subtractor_1_out));  // open: bin, bout
  assign and_1_out = Data_in_1 & Data_in_2;  // AND_Gate and_1, 16 bits wide
  assign xor_1_out = Data_in_1 ^ Data_in_2;  // XOR_Gate xor_1, 16 bits wide
  assign or_1_out = Data_in_1 | Data_in_2;  // OR_Gate or_1, 16 bits wide
  Multiplexer #(.select(5), .width(16), .enable("false")) multiplexer_1 (
    .in12(multiplier_1_out), .in13(divider_1_out), .in16(adder_1_out), .in17(subtractor_1_out),
    .in18(and_1_out), .in19(xor_1_out), .out(multiplexer_1_out), .sel(Select_bit[5:1]));  // open: in0, in1, in2, in3, in4, in5, in6, in7, in8, in9, in10, in11, in14, in15, in20, in21, in22, in23, in24, in25, in26, in27, in28, in29, in30, in31
  Multiplexer #(.select(5), .width(16), .enable("false")) multiplexer_2 (
    .in12(multiplier_1_out), .in13(divider_1_out), .in16(adder_1_out), .in17(subtractor_1_out),
    .in18(or_1_out), .out(multiplexer_2_out), .sel(Select_bit[5:1]));  // open: in0, in1, in2, in3, in4, in5, in6, in7, in8, in9, in10, in11, in14, in15, in19, in20, in21, in22, in23, in24, in25, in26, in27, in28, in29, in30, in31
  Multiplexer #(.width(16), .enable("false")) multiplexer_3 (
    .in0(multiplexer_1_out), .in1(multiplexer_2_out), .out(Data_out), .sel(Select_bit[0]));
endmodule

module PC (
  output [5:0] opcode
);

  wire decoder_1_out2;
  wire [4:0] bit_extender_2_out, undriven_3, undriven_4;
  wire [5:0] undriven_5, undriven_7, undriven_8, undriven_9;
  wire [10:0] undriven;
  wire [13:0] undriven_6;
  wire [15:0] adder_1_out, bit_extender_1_out, register_1_q;
  wire [15:11] undriven_2;
  wire [31:0] undriven_10;

  DotMatrix #(.inputtype("row"), .matrixcols(6), .matrixrows(1)) dotmatrix_1 (.row0(undriven_5));
  DotMatrix #(.inputtype("row"), .matrixcols(6), .matrixrows(1)) dotmatrix_2 (.row0(undriven_9));
  DotMatrix #(.inputtype("row"), .matrixcols(6), .matrixrows(1)) dotmatrix_3 (.row0(undriven_10[31:26]));
  DotMatrix #(.inputtype("row"), .matrixrows(1)) dotmatrix_4 (.row0(undriven_4));
  DotMatrix #(.inputtype("row"), .matrixcols(6), .matrixrows(1)) dotmatrix_5 (.row0(undriven_8));
  DotMatrix #(.inputtype("row"), .matrixcols(26), .matrixrows(1)) dotmatrix_6 (.row0(undriven_10[25:0]));
  DotMatrix #(.inputtype("row"), .matrixrows(1)) dotmatrix_7 (.row0(undriven_3));
  DotMatrix #(.inputtype("row"), .matrixcols(6), .matrixrows(1)) dotmatrix_8 (.row0(undriven_7));
  DotMatrix #(.inputtype("row"), .matrixrows(1)) dotmatrix_9 (.row0(undriven_2));
  DotMatrix #(.inputtype("row"), .matrixcols(11), .matrixrows(1)) dotmatrix_10 (.row0(undriven));
  DotMatrix #(.inputtype("row"), .matrixcols(14), .matrixrows(1)) dotmatrix_11 (.row0(undriven_6));
  Bit_Extender #(.in_width(1)) bit_extender_1 (.out(bit_extender_1_out));  // open: in
  Adder #(.width(16)) adder_1 (.a(register_1_q), .b(bit_extender_1_out), .out(adder_1_out));  // open: cin, cout
  Register #(.width(16)) register_1 (.D(adder_1_out), .Q(register_1_q));  // open: en, clk, clr
  Bit_Extender #(.in_width(6), .out_width(5)) bit_extender_2 (.in(opcode), .out(bit_extender_2_out));
  Decoder #(.select(5), .enable("false")) decoder_1 (
    .out2(decoder_1_out2), .sel(bit_extender_2_out));  // open: out0, out1, out3, out4, out5, out6, out7, out8, out9, out10, out11, out12, out13, out14, out15, out16, out17, out18, out19, out20, out21, out22, out23, out24, out25, out26, out27, out28, out29, out30, out31

  // Notes on the sheet:
  //   Opcode
  //   Opcode
  //   Opcode
  //   rs
  //   rs
  //   rt
  //   fun
  //   Imm
  //   rd
  //   Imm
  //   Imm
endmodule
