// Logisim project Jakarai.circ as structural Verilog: 1 circuit, main circuit main
module main (
  input  in_1,
  output [1:0] rs,
  output [7:0] out_3,
  output [1:0] rt,
  output [7:0] out_5,
  output [7:0] out_6,
  output [7:0] out_7,
  output [7:0] out_8
);

  wire clock_1_out;
  wire [2:0] not_1_out;

  Clock clock_1 (.out(clock_1_out));
  Counter counter_1 (.Q(out_7), .clk(clock_1_out), .clr(in_1));  // open: load, D, count, carry
  RAM ram_1 (.addr(out_7), .data(out_8));  // open: sel, clk, ld, clr
  assign not_1_out = ~out_8[7:5];  // NOT_Gate not_1, 3 bits wide
  RAM #(.addrWidth(2)) ram_2 (.addr(out_8[4:3]), .data(out_3));  // open: sel, clk, ld, clr
  RAM #(.addrWidth(2)) ram_3 (.addr(out_8[2:1]), .data(out_6));  // open: sel, clk, ld, clr
  Adder adder_1 (.a(out_3), .b(out_6), .out(out_5));  // open: cin, cout
  Register register_1 (.D(out_5), .en(not_1_out[0]), .clk(clock_1_out));  // open: Q, clr

  assign rs = out_8[4:3];
  assign rt = out_8[2:1];
endmodule
