// Logisim project Project-1.circ as structural Verilog: 3 circuits, main circuit Final Output
module Decimal_to_BCD (
  input  _9,
  input  _8,
  input  _7,
  input  _6,
  input  _5,
  input  _4,
  input  _3,
  input  _2,
  input  _1,
  input  _0,
  output Y3,
  output Y2,
  output Y1,
  output Y0
);

  or or_1 (Y3, _9, _8);
  or or_2 (Y2, _7, _6, _5, _4);
  or or_3 (Y1, _7, _6, _3, _2);
  or or_4 (Y0, _9, _7, _5, _3, _1);
endmodule

module Final_Output (
  input  Clear,
  output [3:0] out_2,
  output [3:0] out_3,
  output [3:0] out_4,
  output [3:0] out_5,
  output [3:0] out_6
);

  wire _0_out, _1_out, _2_out, _3_out, _4_out, _5_out, _6_out, _7_out, _8_out, _9_out, a, b, c,
       comparator_1_eq, d, decoder_1_out0, decoder_1_out1, decoder_1_out2, decoder_1_out3, decoder_1_out4,
       decoder_1_out6, e, f, g, not_1_out, or_1_out, or_2_out, Set_out;
  wire [2:0] counter_1_q;
  wire [3:0] decimal_to_bcd_1_y0, register_4_q, register_5_q, register_7_q, register_10_q, register_11_q;

  Button _1 (.out(_1_out));
  Button _4 (.out(_4_out));
  Button _7 (.out(_7_out));
  Button _2 (.out(_2_out));
  Button _3 (.out(_3_out));
  Button _5 (.out(_5_out));
  Button _6 (.out(_6_out));
  Button _8 (.out(_8_out));
  Button _9 (.out(_9_out));
  Button _0 (.out(_0_out));
  Button Set (.out(Set_out));
  Decimal_to_BCD decimal_to_bcd_1 (
    .Y3(decimal_to_bcd_1_y0[3]), .Y2(decimal_to_bcd_1_y0[2]), .Y1(decimal_to_bcd_1_y0[1]),
    .Y0(decimal_to_bcd_1_y0[0]), ._9(_9_out), ._8(_8_out), ._6(_6_out), ._5(_5_out), ._4(_4_out),
    ._3(_3_out), ._2(_2_out), ._1(_1_out), ._0(_0_out), ._7(_7_out));
  or or_1 (or_1_out, decimal_to_bcd_1_y0[0], decimal_to_bcd_1_y0[1], _0_out, decimal_to_bcd_1_y0[2], decimal_to_bcd_1_y0[3]);
  Register #(.width(4)) register_1 (.D(decimal_to_bcd_1_y0), .clk(or_1_out), .clr(Clear));  // open: en, Q
  Counter #(.width(3), .max('h7)) counter_1 (
    .Q(counter_1_q), .clk(or_1_out), .clr(or_2_out));  // open: load, D, count, carry
  or or_2 (or_2_out, Clear, Set_out, decoder_1_out6);
  Decoder #(.select(3), .enable("false")) decoder_1 (
    .out0(decoder_1_out0), .out1(decoder_1_out1), .out2(decoder_1_out2), .out3(decoder_1_out3),
    .out4(decoder_1_out4), .out6(decoder_1_out6), .sel(counter_1_q));  // open: out5, out7
  BCD_to_7_seg_decoder bcd_to_7_seg_decoder_1 (
    .A(decimal_to_bcd_1_y0[3]), .B(decimal_to_bcd_1_y0[2]), .C(decimal_to_bcd_1_y0[1]),
    .D(decimal_to_bcd_1_y0[0]), .a_2(a), .b_2(b), .c_2(c), .d_2(d), .e(e), .f(f), .g(g));
  Register #(.width(4)) register_2 (.D(register_4_q), .en(Set_out), .Q(out_2), .clk(Set_out), .clr(Clear));
  Register #(.width(4)) register_3 (.D(register_5_q), .en(Set_out), .Q(out_3), .clk(Set_out), .clr(Clear));
  Register #(.width(4)) register_4 (
    .D(decimal_to_bcd_1_y0), .en(decoder_1_out0), .Q(register_4_q), .clk(or_1_out), .clr(or_2_out));
  Register #(.width(4)) register_5 (
    .D(decimal_to_bcd_1_y0), .en(decoder_1_out1), .Q(register_5_q), .clk(or_1_out), .clr(or_2_out));
  Register #(.width(4)) register_6 (.D(register_7_q), .en(Set_out), .Q(out_4), .clk(Set_out), .clr(Clear));
  Register #(.width(4)) register_7 (
    .D(decimal_to_bcd_1_y0), .en(decoder_1_out2), .Q(register_7_q), .clk(or_1_out), .clr(or_2_out));
  _7_Segment_Display u_7_segment_display_1 (.g(g), .f(f), .a(a), .b(b), .e(e), .d(d), .c(c));  // open: dp
  Register #(.width(4)) register_8 (.D(register_11_q), .en(Set_out), .Q(out_6), .clk(Set_out), .clr(Clear));
  Register #(.width(4)) register_9 (.D(register_10_q), .en(Set_out), .Q(out_5), .clk(Set_out), .clr(Clear));
  Register #(.width(4)) register_10 (
    .D(decimal_to_bcd_1_y0), .en(decoder_1_out3), .Q(register_10_q), .clk(or_1_out), .clr(or_2_out));
  Register #(.width(4)) register_11 (
    .D(decimal_to_bcd_1_y0), .en(decoder_1_out4), .Q(register_11_q), .clk(or_1_out), .clr(or_2_out));
  Comparator #(.width(20)) comparator_1 (
    .a({out_6, out_5, out_4, out_3, out_2}),
    .b({register_11_q, register_10_q, register_7_q, register_5_q, register_4_q}), .eq(comparator_1_eq));  // open: gt, lt
  LED led_1 (.in(comparator_1_eq));
  LED led_2 (.in(not_1_out));
  not not_1 (not_1_out, comparator_1_eq);
  _7_Segment_Display u_7_segment_display_2 (.g(g), .f(f), .a(a), .b(b), .e(e), .d(d), .c(c));  // open: dp

  // Notes on the sheet:
  //   Decimal to BCD
  //   a
  //   b
  //   c
  //   d
  //   e
  //   f
  //   g
  //   BCD to 7 Segment
  //   Correct
  //   Wrong
endmodule

module BCD_to_7_seg_decoder (
  input  A,
  input  B,
  input  C,
  input  D,
  output a_2,
  output b_2,
  output c_2,
  output d_2,
  output e,
  output f,
  output g
);

  wire B_prime_C_out, B_prime_D_prime_out, BC_prime_D_out, BC_prime_out, BD_out, BD_prime_out,
       C_prime_D_prime_out, CD_out, CD_prime_out, not_1_out, not_2_out, not_3_out;

  not not_1 (not_1_out, B);
  not not_2 (not_2_out, D);
  not not_3 (not_3_out, C);
  and BD (BD_out, B, D);
  and B_prime_D_prime (B_prime_D_prime_out, not_1_out, not_2_out);
  and C_prime_D_prime (C_prime_D_prime_out, not_3_out, not_2_out);
  and CD (CD_out, C, D);
  and B_prime_C (B_prime_C_out, not_1_out, C);
  and BC_prime_D (BC_prime_D_out, B, not_3_out, D);
  and CD_prime (CD_prime_out, C, not_2_out);
  and BC_prime (BC_prime_out, B, not_3_out);
  and BD_prime (BD_prime_out, B, not_2_out);
  or u_a (a_2, A, C, BD_out, B_prime_D_prime_out);
  or u_b (b_2, not_1_out, C_prime_D_prime_out, CD_out);
  or u_c (c_2, not_3_out, D, B);
  or u_d (d_2, B_prime_D_prime_out, B_prime_C_out, BC_prime_D_out, CD_prime_out, A);
  or u_e (e, B_prime_D_prime_out, CD_prime_out);
  or u_f (f, C_prime_D_prime_out, BC_prime_out, BD_prime_out, A);
  or u_g (g, B_prime_C_out, BC_prime_out, A, BD_prime_out);

  // Notes on the sheet:
  //   A+C+BD+B'D'
  //   B'+C'D'+CD
  //   C'+D+B
  //   B'D'+B'C+BC'D+CD'+A
  //   B'D'+CD'
  //   C'D'+BC'+BD'+A
  //   B'C+BC'+A+BD'
endmodule
