// Logisim project invite.circ as structural Verilog: 1 circuit, main circuit main
module main (
  input  in_1
);

  wire and_1_out, clock_1_out, not_1_out;
  wire [6:0] rom_1_data;
  wire [7:0] counter_1_q;

  Clock clock_1 (.out(clock_1_out));
  and and_1 (and_1_out, clock_1_out, in_1);
  not not_1 (not_1_out, in_1);
  Counter counter_1 (.Q(counter_1_q), .clk(and_1_out), .clr(not_1_out));  // open: load, D, count, carry
  TTY tty_1 (.data(rom_1_data), .clk(and_1_out), .clr(not_1_out));  // open: we
  ROM #(.dataWidth(7)) rom_1 (.addr(counter_1_q), .data(rom_1_data));  // open: sel

  // Notes on the sheet:
  //   contents of rom_1 (hex, n*v repeats v):
  //   57 69 6c 6c 20 79 6f 75 20 6a 6f 69 6e 20 6d 79 20 74 65 61 6d 3f d a
endmodule
