// Logisim project 2012518642-Md. Ishtiaq Ahamed Fahim-Task 1.circ as structural Verilog: 2 circuits, main circuit main
module main (
  input  [1:0] A1A0,
  input  [1:0] B1B0,
  input  [1:0] S1S0,
  output [1:0] F1F0
);

  ALU2bit alu2bit_1 (.A(A1A0[0]), .B(B1B0[0]), .S1S0(S1S0), .F(F1F0[0]));
  ALU2bit alu2bit_2 (.A(A1A0[1]), .B(B1B0[1]), .S1S0(S1S0), .F(F1F0[1]));
endmodule

module ALU2bit (
  input  A,
  input  B,
  input  [1:0] S1S0,
  output F
);

  wire and_1_out, not_1_out, or_1_out, xor_1_out;

  and and_1 (and_1_out, A, B);
  or or_1 (or_1_out, A, B);
  xor xor_1 (xor_1_out, A, B);
  not not_1 (not_1_out, A);
  Multiplexer #(.select(2), .enable("false")) multiplexer_1 (
    .in0(and_1_out), .in1(or_1_out), .in2(xor_1_out), .in3(not_1_out), .out(F), .sel(S1S0));
endmodule
