// Logisim project 2012518642-Md. Ishtiaq Ahamed Fahim-Task 2.circ as structural Verilog: 2 circuits, main circuit Add,Sub,Inc,Dec,Tras
// Alu-2bit
module Add_Sub_Inc_Dec_Tras (
  input  Cin,
  input  [1:0] S1S0,
  input  A,
  input  B,
  output D,
  output Cout
);

  wire multiplexer_1_out, not_1_out;

  not not_1 (not_1_out, B);
  Multiplexer #(.select(2), .enable("false")) multiplexer_1 (
    .in0(B), .in1(not_1_out), .in2(1'b0), .in3(1'b1), .out(multiplexer_1_out), .sel(S1S0));
  Adder #(.width(1)) adder_1 (.a(A), .b(multiplexer_1_out), .out(D), .cin(Cin), .cout(Cout));

  // Notes on the sheet:
  //   Md. Ishtiaq Ahamed Fahim 2012518642 
endmodule

module main (
  input  Cin,
  input  [1:0] S1S0,
  input  [1:0] A1A0,
  input  [1:0] B1B0,
  output [1:0] D1D0,
  output Cout
);

  wire add_sub_inc_dec_tras_1_cout;

  Add_Sub_Inc_Dec_Tras add_sub_inc_dec_tras_1 (
    .Cin(Cin), .S1S0(S1S0), .A(A1A0[0]), .B(B1B0[0]), .D(D1D0[0]), .Cout(add_sub_inc_dec_tras_1_cout));
  Add_Sub_Inc_Dec_Tras add_sub_inc_dec_tras_2 (
    .Cin(add_sub_inc_dec_tras_1_cout), .S1S0(S1S0), .A(A1A0[1]), .B(B1B0[1]), .D(D1D0[1]), .Cout(Cout));

  // Notes on the sheet:
  //   Md. Ishtiaq Ahamed Fahim 2012518642 
endmodule
