// Logisim project 4 bit multi.circ as structural Verilog: 1 circuit, main circuit main
module main (
  input  [3:0] B,
  input  [3:0] A,
  output [7:0] S
);

  wire [2:0] A2B2_4_out;
  wire [3:0] A1B1_2_out, A1B1_3_out, A1B1_out;
  wire [3:1] adder_1_out, adder_2_out;
  wire [3:3] adder_1_cout, adder_2_cout;

  and A3B3 (A1B1_out[2], A[3], B[2]);
  and A4B4 (A1B1_out[3], A[3], B[3]);
  and A1B1 (A1B1_out[0], A[3], B[0]);
  and A2B2 (A1B1_out[1], A[3], B[1]);
  and A4B4_2 (A1B1_2_out[3], A[2], B[3]);
  and A3B3_2 (A1B1_2_out[2], A[2], B[2]);
  and A2B2_2 (A1B1_2_out[1], A[2], B[1]);
  and A1B1_2 (A1B1_2_out[0], A[2], B[0]);
  and A4B4_3 (A1B1_3_out[3], A[1], B[3]);
  and A3B3_3 (A1B1_3_out[2], A[1], B[2]);
  and A2B2_3 (A1B1_3_out[1], A[1], B[1]);
  and A1B1_3 (A1B1_3_out[0], A[1], B[0]);
  and A4B4_4 (A2B2_4_out[2], A[0], B[3]);
  and A3B3_4 (A2B2_4_out[1], A[0], B[2]);
  and A2B2_4 (A2B2_4_out[0], A[0], B[1]);
  and A1B1_4 (S[0], A[0], B[0]);
  Adder #(.width(4)) adder_1 (
    .a({1'b0, A2B2_4_out}), .b(A1B1_3_out), .out({adder_1_out, S[1]}), .cin(1'b0), .cout(adder_1_cout[3]));
  Adder #(.width(4)) adder_2 (
    .a({adder_1_cout[3], adder_1_out}), .b(A1B1_2_out), .out({adder_2_out, S[2]}), .cin(1'b0),
    .cout(adder_2_cout[3]));
  Adder #(.width(4)) adder_3 (.a({adder_2_cout[3], adder_2_out}), .b(A1B1_out), .out(S[6:3]), .cin(1'b0), .cout(S[7]));
endmodule
