// Logisim project 2012518642-Md. Ishtiaq Ahamed Fahim- Task 6.circ as structural Verilog: 3 circuits, main circuit main
module main (
  input  [15:0] Write_Data,
  input  [3:0] RS,
  input  [3:0] RD,
  input  WE,
  input  [3:0] RT,
  input  Clock,
  output [15:0] Data1,
  output [15:0] Data2
);

  wire and_1_out, and_2_out, and_3_out, and_4_out, and_5_out, and_6_out, and_7_out, and_8_out, and_9_out,
       and_10_out, and_11_out, and_12_out, and_13_out, and_14_out, and_15_out, and_16_out, decoder_1_out0,
       decoder_1_out1, decoder_1_out2, decoder_1_out3, decoder_1_out4, decoder_1_out5, decoder_1_out6,
       decoder_1_out7, decoder_1_out8, decoder_1_out9, decoder_1_out10, decoder_1_out11, decoder_1_out12,
       decoder_1_out13, decoder_1_out14, decoder_1_out15;
  wire [15:0] _13_q, R0_q, R1_q, R2_q, R3_q, R4_q, R5_q, R6_q, R7_q, R8_q, R9_q, R10_q, R11_q, R12_q, R14_q,
       R15_q;

  Decoder #(.select(4), .enable("false")) decoder_1 (
    .out0(decoder_1_out0), .out1(decoder_1_out1), .out2(decoder_1_out2), .out3(decoder_1_out3),
    .out4(decoder_1_out4), .out5(decoder_1_out5), .out6(decoder_1_out6), .out7(decoder_1_out7),
    .out8(decoder_1_out8), .out9(decoder_1_out9), .out10(decoder_1_out10), .out11(decoder_1_out11),
    .out12(decoder_1_out12), .out13(decoder_1_out13), .out14(decoder_1_out14), .out15(decoder_1_out15),
    .sel(RD));
  and and_1 (and_1_out, decoder_1_out0, WE);
  and and_2 (and_2_out, decoder_1_out1, WE);
  and and_3 (and_3_out, decoder_1_out2, WE);
  and and_4 (and_4_out, decoder_1_out3, WE);
  and and_5 (and_5_out, decoder_1_out4, WE);
  and and_6 (and_6_out, decoder_1_out5, WE);
  and and_7 (and_7_out, decoder_1_out6, WE);
  and and_8 (and_8_out, decoder_1_out7, WE);
  Register #(.width(16)) R0 (.D(Write_Data), .en(and_1_out), .Q(R0_q), .clk(Clock));  // open: clr
  Register #(.width(16)) R1 (.D(Write_Data), .en(and_2_out), .Q(R1_q), .clk(Clock));  // open: clr
  Register #(.width(16)) R2 (.D(Write_Data), .en(and_3_out), .Q(R2_q), .clk(Clock));  // open: clr
  Register #(.width(16)) R3 (.D(Write_Data), .en(and_4_out), .Q(R3_q), .clk(Clock));  // open: clr
  Register #(.width(16)) R4 (.D(Write_Data), .en(and_5_out), .Q(R4_q), .clk(Clock));  // open: clr
  Register #(.width(16)) R5 (.D(Write_Data), .en(and_6_out), .Q(R5_q), .clk(Clock));  // open: clr
  Register #(.width(16)) R6 (.D(Write_Data), .en(and_7_out), .Q(R6_q), .clk(Clock));  // open: clr
  Register #(.width(16)) R7 (.D(Write_Data), .en(and_8_out), .Q(R7_q), .clk(Clock));  // open: clr
  and and_9 (and_9_out, decoder_1_out8, WE);
  and and_10 (and_10_out, decoder_1_out9, WE);
  and and_11 (and_11_out, decoder_1_out10, WE);
  and and_12 (and_12_out, decoder_1_out11, WE);
  and and_13 (and_13_out, decoder_1_out12, WE);
  and and_14 (and_14_out, decoder_1_out13, WE);
  and and_15 (and_15_out, decoder_1_out14, WE);
  and and_16 (and_16_out, decoder_1_out15, WE);
  Register #(.width(16)) R8 (.D(Write_Data), .en(and_9_out), .Q(R8_q), .clk(Clock));  // open: clr
  Register #(.width(16)) R9 (.D(Write_Data), .en(and_10_out), .Q(R9_q), .clk(Clock));  // open: clr
  Register #(.width(16)) R10 (.D(Write_Data), .en(and_11_out), .Q(R10_q), .clk(Clock));  // open: clr
  Register #(.width(16)) R11 (.D(Write_Data), .en(and_12_out), .Q(R11_q), .clk(Clock));  // open: clr
  Register #(.width(16)) R12 (.D(Write_Data), .en(and_13_out), .Q(R12_q), .clk(Clock));  // open: clr
  Register #(.width(16)) _13 (.D(Write_Data), .en(and_14_out), .Q(_13_q), .clk(Clock));  // open: clr
  Register #(.width(16)) R14 (.D(Write_Data), .en(and_15_out), .Q(R14_q), .clk(Clock));  // open: clr
  Register #(.width(16)) R15 (.D(Write_Data), .en(and_16_out), .Q(R15_q), .clk(Clock));  // open: clr
  Multiplexer #(.select(4), .width(16), .enable("false")) multiplexer_1 (
    .in0(R0_q), .in1(R1_q), .in2(R2_q), .in3(R3_q), .in4(R4_q), .in5(R5_q), .in6(R6_q), .in7(R7_q),
    .in8(R8_q), .in9(R9_q), .in10(R10_q), .in11(R11_q), .in12(R12_q), .in13(_13_q), .in14(R14_q),
    .in15(R15_q), .out(Data1), .sel(RS));
  Multiplexer #(.select(4), .width(16), .enable("false")) multiplexer_2 (
    .in0(R0_q), .in1(R1_q), .in2(R2_q), .in3(R3_q), .in4(R4_q), .in5(R5_q), .in6(R6_q), .in7(R7_q),
    .in8(R8_q), .in9(R9_q), .in10(R10_q), .in11(R11_q), .in12(R12_q), .in13(_13_q), .in14(R14_q),
    .in15(R15_q), .out(Data2), .sel(RT));
endmodule

module Task (
  input  [3:0] in_1,
  input  in_2,
  output [3:0] OP_Code,
  output [3:0] RS,
  output [3:0] RT__Rd,
  output [3:0] Imm
);

  wire clock_1_out;
  wire [15:0] adder_1_out, alu_1_data_out, bit_extender_1_out, main_1_data1, main_1_data2, register_1_q;

  Register #(.width(16)) register_1 (.D(adder_1_out), .Q(register_1_q), .clk(clock_1_out));  // open: en, clr
  Clock clock_1 (.out(clock_1_out));
  assign bit_extender_1_out = {{15{1'b0}}, 1'b1};  // Bit_Extender bit_extender_1
  Adder #(.width(16)) adder_1 (.a(register_1_q), .b(bit_extender_1_out), .out(adder_1_out));  // open: cin, cout
  ROM #(.addrWidth(16), .dataWidth(16)) rom_1 (.addr(register_1_q), .data({OP_Code, RS, RT__Rd, Imm}));  // open: sel
  main main_1 (
    .Write_Data(alu_1_data_out), .RD(Imm), .WE(in_2), .Data1(main_1_data1), .RS(RS), .Data2(main_1_data2),
    .RT(RT__Rd), .Clock(clock_1_out));
  ALU alu_1 (.Data_in_1(main_1_data1), .Data_in_2(main_1_data2), .Select_bit(in_1), .Data_out(alu_1_data_out));

  // Notes on the sheet:
  //   contents of rom_1 (hex, n*v repeats v):
  //   234
  //   Md. Ishtiaq Ahamed Fahim 2012518642
endmodule

// 16 ALU
module ALU (
  input  [15:0] Data_in_1,
  input  [15:0] Data_in_2,
  input  [3:0] Select_bit,
  output [15:0] Data_out
);

  wire [15:0] adder_1_out, and_1_out, nor_1_out, not_1_out, or_1_out, subtractor_1_out;

  Adder #(.width(16)) adder_1 (.a(Data_in_1), .b(Data_in_2), .out(adder_1_out));  // open: cin, cout
  Subtractor #(.width(16)) subtractor_1 (.a(Data_in_1), .b(Data_in_2), .out(subtractor_1_out));  // open: bin, bout
  assign and_1_out = Data_in_1 & Data_in_2;  // AND_Gate and_1, 16 bits wide
  assign or_1_out = Data_in_1 | Data_in_2;  // OR_Gate or_1, 16 bits wide
  assign nor_1_out = ~(Data_in_1 | Data_in_2);  // NOR_Gate nor_1, 16 bits wide
  assign not_1_out = ~Data_in_1;  // NOT_Gate not_1, 16 bits wide
  Multiplexer #(.select(4), .width(16), .enable("false")) multiplexer_1 (
    .in0(adder_1_out), .in1(subtractor_1_out), .in2(and_1_out), .in3(or_1_out), .in4(nor_1_out),
    .in5(not_1_out), .out(Data_out), .sel(Select_bit));  // open: in6, in7, in8, in9, in10, in11, in12, in13, in14, in15
endmodule
