// Logisim project 2012518642-Md. Ishtiaq Ahamed Fahim-Task 7.circ as structural Verilog: 2 circuits, main circuit main
// 16 bit regester
module _16_bit_regester (
  input  [15:0] Data_in,
  input  [3:0] rs,
  input  [3:0] rd,
  input  unable,
  input  [3:0] rt,
  input  Clock,
  output [15:0] Data_out_1,
  output [15:0] Data_out_2
);

  wire and_1_out, and_2_out, and_3_out, and_4_out, and_5_out, and_6_out, and_7_out, and_8_out, and_9_out,
       and_10_out, and_11_out, and_12_out, and_13_out, and_14_out, and_15_out, and_16_out, decoder_1_out0,
       decoder_1_out1, decoder_1_out2, decoder_1_out3, decoder_1_out4, decoder_1_out5, decoder_1_out6,
       decoder_1_out7, decoder_1_out8, decoder_1_out9, decoder_1_out10, decoder_1_out11, decoder_1_out12,
       decoder_1_out13, decoder_1_out14, decoder_1_out15;
  wire [15:0] R0_q, R1_q, R2_q, R3_q, R4_q, R5_q, R6_q, R7_q, R8_q, R9_q, R10_q, R11_q, R12_q, R13_q, R14_q,
       R15_q;

  Decoder #(.select(4), .enable("false")) decoder_1 (
    .out0(decoder_1_out0), .out1(decoder_1_out1), .out2(decoder_1_out2), .out3(decoder_1_out3),
    .out4(decoder_1_out4), .out5(decoder_1_out5), .out6(decoder_1_out6), .out7(decoder_1_out7),
    .out8(decoder_1_out8), .out9(decoder_1_out9), .out10(decoder_1_out10), .out11(decoder_1_out11),
    .out12(decoder_1_out12), .out13(decoder_1_out13), .out14(decoder_1_out14), .out15(decoder_1_out15),
    .sel(rd));
  and and_1 (and_1_out, decoder_1_out0, unable);
  and and_2 (and_2_out, decoder_1_out1, unable);
  and and_3 (and_3_out, decoder_1_out2, unable);
  and and_4 (and_4_out, decoder_1_out3, unable);
  and and_5 (and_5_out, decoder_1_out4, unable);
  and and_6 (and_6_out, decoder_1_out5, unable);
  and and_7 (and_7_out, decoder_1_out6, unable);
  and and_8 (and_8_out, decoder_1_out7, unable);
  Register #(.width(16)) R0 (.D(Data_in), .en(and_1_out), .Q(R0_q), .clk(Clock));  // open: clr
  Register #(.width(16)) R1 (.D(Data_in), .en(and_2_out), .Q(R1_q), .clk(Clock));  // open: clr
  Register #(.width(16)) R2 (.D(Data_in), .en(and_3_out), .Q(R2_q), .clk(Clock));  // open: clr
  Register #(.width(16)) R3 (.D(Data_in), .en(and_4_out), .Q(R3_q), .clk(Clock));  // open: clr
  Register #(.width(16)) R4 (.D(Data_in), .en(and_5_out), .Q(R4_q), .clk(Clock));  // open: clr
  Register #(.width(16)) R5 (.D(Data_in), .en(and_6_out), .Q(R5_q), .clk(Clock));  // open: clr
  Register #(.width(16)) R6 (.D(Data_in), .en(and_7_out), .Q(R6_q), .clk(Clock));  // open: clr
  Register #(.width(16)) R7 (.D(Data_in), .en(and_8_out), .Q(R7_q), .clk(Clock));  // open: clr
  and and_9 (and_9_out, decoder_1_out8, unable);
  and and_10 (and_10_out, decoder_1_out9, unable);
  and and_11 (and_11_out, decoder_1_out10, unable);
  and and_12 (and_12_out, decoder_1_out11, unable);
  and and_13 (and_13_out, decoder_1_out12, unable);
  and and_14 (and_14_out, decoder_1_out13, unable);
  and and_15 (and_15_out, decoder_1_out14, unable);
  and and_16 (and_16_out, decoder_1_out15, unable);
  Register #(.width(16)) R8 (.D(Data_in), .en(and_9_out), .Q(R8_q), .clk(Clock));  // open: clr
  Register #(.width(16)) R9 (.D(Data_in), .en(and_10_out), .Q(R9_q), .clk(Clock));  // open: clr
  Register #(.width(16)) R10 (.D(Data_in), .en(and_11_out), .Q(R10_q), .clk(Clock));  // open: clr
  Register #(.width(16)) R11 (.D(Data_in), .en(and_12_out), .Q(R11_q), .clk(Clock));  // open: clr
  Register #(.width(16)) R12 (.D(Data_in), .en(and_13_out), .Q(R12_q), .clk(Clock));  // open: clr
  Register #(.width(16)) R13 (.D(Data_in), .en(and_14_out), .Q(R13_q), .clk(Clock));  // open: clr
  Register #(.width(16)) R14 (.D(Data_in), .en(and_15_out), .Q(R14_q), .clk(Clock));  // open: clr
  Register #(.width(16)) R15 (.D(Data_in), .en(and_16_out), .Q(R15_q), .clk(Clock));  // open: clr
  Multiplexer #(.select(4), .width(16), .enable("false")) multiplexer_1 (
    .in0(R0_q), .in1(R1_q), .in2(R2_q), .in3(R3_q), .in4(R4_q), .in5(R5_q), .in6(R6_q), .in7(R7_q),
    .in8(R8_q), .in9(R9_q), .in10(R10_q), .in11(R11_q), .in12(R12_q), .in13(R13_q), .in14(R14_q),
    .in15(R15_q), .out(Data_out_1), .sel(rs));
  Multiplexer #(.select(4), .width(16), .enable("false")) multiplexer_2 (
    .in0(R0_q), .in1(R1_q), .in2(R2_q), .in3(R3_q), .in4(R4_q), .in5(R5_q), .in6(R6_q), .in7(R7_q),
    .in8(R8_q), .in9(R9_q), .in10(R10_q), .in11(R11_q), .in12(R12_q), .in13(R13_q), .in14(R14_q),
    .in15(R15_q), .out(Data_out_2), .sel(rt));

  // Notes on the sheet:
  //   Md. Ishtiaq Ahamed Fahim 2012518642
endmodule

module main (
  input  On,
  output [15:0] out_2,
  output [15:0] out_3,
  output [15:0] out_4
);

  wire and_1_out, Clock_out, not_1_out, not_2_out;
  wire [3:0] adder_2_out;
  wire [7:0] adder_1_out, bit_extender_1_out, register_1_q;
  wire [15:0] rom_1_data;

  Clock Clock (.out(Clock_out));
  and and_1 (and_1_out, Clock_out, On);
  not not_1 (not_1_out, On);
  Adder adder_1 (.a(register_1_q), .b(bit_extender_1_out), .out(adder_1_out));  // open: cin, cout
  assign bit_extender_1_out = {{7{1'b0}}, On};  // Bit_Extender bit_extender_1
  ROM #(.dataWidth(16)) rom_1 (.addr(register_1_q), .data(rom_1_data), .sel(On));
  Register register_1 (.D(adder_1_out), .Q(register_1_q), .clk(and_1_out), .clr(not_1_out));  // open: en
  DotMatrix #(.inputtype("row"), .matrixcols(4), .matrixrows(1)) dotmatrix_1 (.row0(rom_1_data[15:12]));
  DotMatrix #(.inputtype("row"), .matrixcols(4), .matrixrows(1)) dotmatrix_2 (.row0(rom_1_data[11:8]));
  DotMatrix #(.inputtype("row"), .matrixcols(4), .matrixrows(1)) dotmatrix_3 (.row0(rom_1_data[7:4]));
  not not_2 (not_2_out, rom_1_data[12]);
  DotMatrix #(.inputtype("row"), .matrixcols(4), .matrixrows(1)) dotmatrix_4 (.row0(rom_1_data[3:0]));
  Adder #(.width(4)) adder_2 (.a(rom_1_data[3:0]), .b(rom_1_data[7:4]), .out(adder_2_out));  // open: cin, cout
  _16_bit_regester u_16_bit_regester_1 (
    .Data_in(out_2), .rd(rom_1_data[11:8]), .unable(not_2_out), .Clock(and_1_out), .Data_out_1(out_3),
    .rs(rom_1_data[11:8]), .Data_out_2(out_4));  // open: rt
  RAM #(.addrWidth(4), .dataWidth(16), .bus("separate")) ram_1 (
    .addr(adder_2_out), .din(out_3), .data(out_2), .str(rom_1_data[12]), .sel(On), .clk(and_1_out));  // open: ld, clr

  // Notes on the sheet:
  //   contents of rom_1 (hex, n*v repeats v):
  //   1021 121
  //   Opcode
  //   rs
  //   Md. Ishtiaq Ahamed Fahim 2012518642
  //   rd
  //   Imm
endmodule
